# Fritzing sketch powermeterPeripheral (saved by Fritzing 0.9.4)
perfboards: 4

parts:
  Part1 = Arduino Nano (Rev3.0)  # not connected
  U1 = 7-SEGMENT-4DIGIT [package=7-segment-4digit_longpads_for_pogobed]  # not connected
  U2 = 7-SEGMENT-4DIGIT [package=7-segment-4digit_longpads_for_pogobed]  # not connected
  U3 = 7-SEGMENT-4DIGIT [package=7-segment-4digit_longpads_for_pogobed]  # not connected
  R7 = Resistor [tolerance=±5% resistance=75 package=THT]  # not connected
  R1 = Resistor [tolerance=±5% resistance=75 package=THT]  # not connected
  R2 = Resistor [tolerance=±5% resistance=75 package=THT]  # not connected
  R8 = Resistor [tolerance=±5% resistance=75 package=THT]  # not connected
  R6 = Resistor [tolerance=±5% resistance=75 package=THT]  # not connected
  R9 = Resistor [tolerance=±5% resistance=75 package=THT]  # not connected
  R10 = Resistor [tolerance=±5% resistance=75 package=THT]  # not connected
  Part2 = Arduino Nano (Rev3.0)  # not connected
  U4 = 7-SEGMENT-4DIGIT [package=7-segment-4digit_longpads_for_pogobed]
  U5 = 7-SEGMENT-4DIGIT [package=7-segment-4digit_longpads_for_pogobed]
  U6 = 7-SEGMENT-4DIGIT [package=7-segment-4digit_longpads_for_pogobed]

nets:
  N1: U4.14, U5.14, U6.14
  N2: U4.15, U5.15
