# Fritzing sketch powermeterSensor (saved by Fritzing 0.9.4)
breadboards: 1
perfboards: 1

parts:
  Part1 = NANO 33 BLE
  BAT2 = Battery Holders [package=battcom_20mm_pth]
  R1 = Resistor [tolerance=±5% resistance=220 package=THT]
  R2 = Resistor [tolerance=±5% resistance=220 package=THT]
  R3 = Resistor [tolerance=±5% resistance=220 package=THT]
  R4 = Resistor [tolerance=±5% resistance=220 package=THT]
  Part2 = HX711 Weighing Sensor Module
  Part6 = HX711 Weighing Sensor Module
  Part7 = Arduino Nano (Rev3.0) (ICSP)

nets (from the breadboard view):
  GND: Part1.GND, BAT2.+, Part2.GND
  N1: Part1.D2, Part2.DO/RX
  N2: Part1.D3~, Part2.CK/TX
  N3: Part1.VIN, BAT2.-
  3V3: Part1.3V3, Part2.VCC
  N4: R1.Pin_1, R3.Pin_0, Part2.E+
  N5: R2.Pin_1, Part2.A-
  N6: R4.Pin_0, Part2.A+
  N7: R4.Pin_1, Part2.E-
  VCC: Part6.VCC, Part7.3V3
  GND_2: Part6.GND, Part7.GND
  N8: Part6.DO/RX, Part7.A1
  N9: Part6.CK/TX, Part7.A0
  N10: Part7.VIN, Part7.A2

custom parts:
  NANO 33 BLE: This compact and reliable Nano board is built around the NINA B306 module, based on Nordic nRF 52840 and containing a powerful Cortex M4F. Its architecture, fully compatible with Arduino IDE Online and Offline, has a 9 axis Inertial Measurement Unit (IMU) and a reduced power consumption compared to other same size boards. This allows the design of wearable devices and movement sensing projects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
